// Logisim project test.circ as structural Verilog: 4 circuits, main circuit Partie 1 | D.A
module Partie_1___D_A (
  input  A,
  input  B,
  output Retenue,
  output Somme
);

  and and_1 (Retenue, A, B);
  xor xor_1 (Somme, A, B);
endmodule

module Partie_2___additionneur_1_bit (
  input  A,
  input  B,
  input  Re,
  output S,
  output Rs
);

  wire and_1_out, and_2_out, xor_1_out;

  xor xor_1 (xor_1_out, A, B);
  xor xor_2 (S, xor_1_out, Re);
  and and_1 (and_1_out, Re, xor_1_out);
  and and_2 (and_2_out, B, A);
  or or_1 (Rs, and_1_out, and_2_out);
endmodule

module Partie_3___additionneur_2_bits (
  input  b0,
  input  b1,
  input  a0,
  input  a1,
  input  re,
  output s0,
  output s1,
  output rs
);

  wire partie_2_additionneur_1_bit_1_rs;

  Partie_2___additionneur_1_bit partie_2_additionneur_1_bit_1 (
    .A(a0), .B(a1), .Re(re), .S(s0), .Rs(partie_2_additionneur_1_bit_1_rs));
  Partie_2___additionneur_1_bit partie_2_additionneur_1_bit_2 (
    .A(b0), .B(b1), .Re(partie_2_additionneur_1_bit_1_rs), .S(s1), .Rs(rs));
endmodule

module Additionneur_2_bits (
  input  B0,
  input  Re,
  input  A0,
  input  B1,
  input  Rs0,
  input  A1,
  output S0,
  output Rs,
  output S1,
  output S0_2,
  output Rs_2,
  output S1_2,
  output Rs_3
);

  // AND_Gate and_1 is placed but not wired
  // AND_Gate and_2 is placed but not wired
  // XOR_Gate xor_1: pin names not known; wires that end beside it: A0, B1, Rs0
  // XOR_Gate xor_2 has open pins: in2=A1, out=open
endmodule
